// Logisim project circ 2.circ as structural Verilog: 1 circuit, main circuit main
module main (
  input  S1,
  input  S2,
  input  S3,
  input  S4,
  input  S5,
  output F,
  output C,
  output M
);

  wire and_1_out, and_2_out, and_3_out, and_4_out, and_5_out, and_6_out, or_1_out, or_2_out;

  and and_1 (and_1_out, S3, S1);
  and and_2 (and_2_out, S4, S1);
  and and_3 (and_3_out, S1, S2);
  and and_4 (and_4_out, S3, S4);
  and and_5 (and_5_out, S2, S3);
  and and_6 (and_6_out, S2, S4);
  or or_1 (or_1_out, and_1_out, and_2_out, and_3_out, and_4_out, and_5_out, and_6_out);
  or or_2 (or_2_out, or_1_out, S5);
  and and_7 (C, or_1_out, S5);
  not not_1 (F, or_2_out);

  assign M = S5;
endmodule
