// Logisim project comparador.circ as structural Verilog: 1 circuit, main circuit main
module main (
  input  A,
  input  B,
  output Igual,
  output menor,
  output maior
);

  wire not_1_out, not_2_out;

  not not_1 (not_1_out, A);
  not not_2 (not_2_out, B);
  xnor xnor_1 (Igual, A, B);
  and and_1 (menor, not_1_out, B);
  and and_2 (maior, A, not_2_out);
endmodule
