// Logisim project fusão somador subtrator.circ as structural Verilog: 4 circuits, main circuit main
module main (
  input  in_1,
  input  [7:0] in_2,
  input  [7:0] in_3,
  output [8:0] out_4
);

  wire cross_adder_subtractor_1_cout, cross_adder_subtractor_2_cout, not_1_out;

  cross_adder_subtractor cross_adder_subtractor_1 (
    .A(in_2[3:0]), .B(in_3[3:0]), .S(out_4[3:0]), .switch(not_1_out), .cin(in_1),
    .cout(cross_adder_subtractor_1_cout));
  cross_adder_subtractor cross_adder_subtractor_2 (
    .A(in_2[7:4]), .B(in_3[7:4]), .S(out_4[7:4]), .switch(not_1_out), .cin(cross_adder_subtractor_1_cout),
    .cout(cross_adder_subtractor_2_cout));
  not not_1 (not_1_out, in_1);
  Multiplexer multiplexer_1 (
    .in0(not_1_out), .in1(cross_adder_subtractor_2_cout), .out(out_4[8]), .sel(not_1_out), .en(1'b1));

  // Other names for the same wires on the sheet: a0[3:0] = in_2[3:0]; a1[3:0] = in_2[7:4]; b0[3:0] = in_3[3:0];
  //   b1[3:0] = in_3[7:4]

  // Notes on the sheet:
  //   somador / subtrator de 8 bits
endmodule

module half_adder (
  input  a,
  input  b,
  output s,
  output cout
);

  xor xor_1 (s, a, b);
  and and_1 (cout, a, b);

  // Notes on the sheet:
  //   meio somador
endmodule

module full_adder (
  input  Cin,
  input  a,
  input  b,
  output S,
  output Cout
);

  wire half_adder_1_cout, half_adder_2_cout, half_adder_2_s;

  half_adder half_adder_1 (.a(Cin), .b(half_adder_2_s), .s(S), .cout(half_adder_1_cout));
  half_adder half_adder_2 (.a(a), .b(b), .s(half_adder_2_s), .cout(half_adder_2_cout));
  or or_1 (Cout, half_adder_1_cout, half_adder_2_cout);

  // Notes on the sheet:
  //   somador completo
endmodule

module cross_adder_subtractor (
  input  switch,
  input  cin,
  input  [3:0] A,
  input  [3:0] B,
  output [3:0] S,
  output cout
);

  wire full_adder_1_cout, full_adder_2_cout, full_adder_3_cout, xnor_1_out, xnor_2_out, xnor_3_out,
       xnor_4_out;

  xnor xnor_1 (xnor_1_out, switch, B[0]);
  xnor xnor_2 (xnor_2_out, switch, B[1]);
  xnor xnor_3 (xnor_3_out, switch, B[2]);
  xnor xnor_4 (xnor_4_out, switch, B[3]);
  full_adder full_adder_1 (.Cin(cin), .a(A[0]), .b(xnor_1_out), .S(S[0]), .Cout(full_adder_1_cout));
  full_adder full_adder_2 (.Cin(full_adder_1_cout), .a(A[1]), .b(xnor_2_out), .S(S[1]), .Cout(full_adder_2_cout));
  full_adder full_adder_3 (.Cin(full_adder_2_cout), .a(A[2]), .b(xnor_3_out), .S(S[2]), .Cout(full_adder_3_cout));
  full_adder full_adder_4 (.Cin(full_adder_3_cout), .a(A[3]), .b(xnor_4_out), .S(S[3]), .Cout(cout));

  // Notes on the sheet:
  //   somador / subtrator de 4 bits 
endmodule
