// Logisim project relógio E e M.circ as structural Verilog: 5 circuits, main circuit main
module main (
  input  in_1
);

  wire and_1_out, and_2_out, and_3_out, clock_1_out, contador_0_5_1_q, contador_0_5_2_q, contador_0_9_1_q,
       contador_0_9_2_q, contador_0_9_3_q, lut_bcd_7seg_1_out_2, lut_bcd_7seg_1_out_3, lut_bcd_7seg_1_out_4,
       lut_bcd_7seg_1_out_5, lut_bcd_7seg_1_out_6, lut_bcd_7seg_1_out_7, lut_bcd_7seg_1_out_8,
       lut_bcd_7seg_2_out_2, lut_bcd_7seg_2_out_3, lut_bcd_7seg_2_out_4, lut_bcd_7seg_2_out_5,
       lut_bcd_7seg_2_out_6, lut_bcd_7seg_2_out_7, lut_bcd_7seg_2_out_8, lut_bcd_7seg_3_out_2,
       lut_bcd_7seg_3_out_3, lut_bcd_7seg_3_out_4, lut_bcd_7seg_3_out_5, lut_bcd_7seg_3_out_6,
       lut_bcd_7seg_3_out_7, lut_bcd_7seg_3_out_8, lut_bcd_7seg_4_out_2, lut_bcd_7seg_4_out_3,
       lut_bcd_7seg_4_out_4, lut_bcd_7seg_4_out_5, lut_bcd_7seg_4_out_6, lut_bcd_7seg_4_out_7,
       lut_bcd_7seg_4_out_8, lut_bcd_7seg_5_out_2, lut_bcd_7seg_5_out_3, lut_bcd_7seg_5_out_4,
       lut_bcd_7seg_5_out_5, lut_bcd_7seg_5_out_6, lut_bcd_7seg_5_out_7, lut_bcd_7seg_5_out_8,
       lut_bcd_7seg_6_out_2, lut_bcd_7seg_6_out_3, lut_bcd_7seg_6_out_4, lut_bcd_7seg_6_out_5,
       lut_bcd_7seg_6_out_6, lut_bcd_7seg_6_out_7, lut_bcd_7seg_6_out_8, xor_1_out;
  wire [1:0] H2;
  wire [2:0] M2, S2;
  wire [3:0] H, M, S;

  lut_BCD_7seg lut_bcd_7seg_1 (
    .out_2(lut_bcd_7seg_1_out_2), .out_3(lut_bcd_7seg_1_out_3), .out_4(lut_bcd_7seg_1_out_4),
    .out_5(lut_bcd_7seg_1_out_5), .out_6(lut_bcd_7seg_1_out_6), .out_7(lut_bcd_7seg_1_out_7),
    .out_8(lut_bcd_7seg_1_out_8), .in_1({2'b00, H2}));
  _7_Segment_Display u_7_segment_display_1 (
    .g(lut_bcd_7seg_1_out_2), .f(lut_bcd_7seg_1_out_3), .a(lut_bcd_7seg_1_out_4), .b(lut_bcd_7seg_1_out_5),
    .e(lut_bcd_7seg_1_out_6), .d(lut_bcd_7seg_1_out_7), .c(lut_bcd_7seg_1_out_8));  // open: dp
  Clock clock_1 (.out(clock_1_out));
  lut_BCD_7seg lut_bcd_7seg_2 (
    .out_2(lut_bcd_7seg_2_out_2), .out_3(lut_bcd_7seg_2_out_3), .out_4(lut_bcd_7seg_2_out_4),
    .out_5(lut_bcd_7seg_2_out_5), .out_6(lut_bcd_7seg_2_out_6), .out_7(lut_bcd_7seg_2_out_7),
    .out_8(lut_bcd_7seg_2_out_8), .in_1(H));
  _7_Segment_Display u_7_segment_display_2 (
    .g(lut_bcd_7seg_2_out_2), .f(lut_bcd_7seg_2_out_3), .a(lut_bcd_7seg_2_out_4), .b(lut_bcd_7seg_2_out_5),
    .e(lut_bcd_7seg_2_out_6), .d(lut_bcd_7seg_2_out_7), .c(lut_bcd_7seg_2_out_8));  // open: dp
  _7_Segment_Display u_7_segment_display_3 (
    .g(lut_bcd_7seg_4_out_2), .f(lut_bcd_7seg_4_out_3), .a(lut_bcd_7seg_4_out_4), .b(lut_bcd_7seg_4_out_5),
    .e(lut_bcd_7seg_4_out_6), .d(lut_bcd_7seg_4_out_7), .c(lut_bcd_7seg_4_out_8));  // open: dp
  contador_0___9 contador_0_9_1 (
    .clock(clock_1_out), .Q(contador_0_9_1_q), .Q0(S[0]), .Q1(S[1]), .Q2(S[2]), .Q3(S[3]), .clear(xor_1_out));
  contador_0___5 contador_0_5_1 (
    .clock(contador_0_9_1_q), .Q(contador_0_5_1_q), .Q0(S2[0]), .Q1(S2[1]), .Q2(S2[2]), .clear(xor_1_out));
  contador_0___9 contador_0_9_2 (
    .clock(contador_0_5_1_q), .Q(contador_0_9_2_q), .Q0(M[0]), .Q1(M[1]), .Q2(M[2]), .Q3(M[3]),
    .clear(xor_1_out));
  contador_0___5 contador_0_5_2 (
    .clock(contador_0_9_2_q), .Q(contador_0_5_2_q), .Q0(M2[0]), .Q1(M2[1]), .Q2(M2[2]), .clear(xor_1_out));
  contador_0___9 contador_0_9_3 (
    .clock(contador_0_5_2_q), .Q(contador_0_9_3_q), .Q0(H[0]), .Q1(H[1]), .Q2(H[2]), .Q3(H[3]),
    .clear(xor_1_out));
  contador_0___2 contador_0_2_1 (.clock(contador_0_9_3_q), .Q0(H2[0]), .Q1(H2[1]), .clear(xor_1_out));  // open: Q
  lut_BCD_7seg lut_bcd_7seg_3 (
    .out_2(lut_bcd_7seg_3_out_2), .out_3(lut_bcd_7seg_3_out_3), .out_4(lut_bcd_7seg_3_out_4),
    .out_5(lut_bcd_7seg_3_out_5), .out_6(lut_bcd_7seg_3_out_6), .out_7(lut_bcd_7seg_3_out_7),
    .out_8(lut_bcd_7seg_3_out_8), .in_1(M));
  lut_BCD_7seg lut_bcd_7seg_4 (
    .out_2(lut_bcd_7seg_4_out_2), .out_3(lut_bcd_7seg_4_out_3), .out_4(lut_bcd_7seg_4_out_4),
    .out_5(lut_bcd_7seg_4_out_5), .out_6(lut_bcd_7seg_4_out_6), .out_7(lut_bcd_7seg_4_out_7),
    .out_8(lut_bcd_7seg_4_out_8), .in_1({1'b0, M2}));
  _7_Segment_Display u_7_segment_display_4 (
    .g(lut_bcd_7seg_3_out_2), .f(lut_bcd_7seg_3_out_3), .a(lut_bcd_7seg_3_out_4), .b(lut_bcd_7seg_3_out_5),
    .e(lut_bcd_7seg_3_out_6), .d(lut_bcd_7seg_3_out_7), .c(lut_bcd_7seg_3_out_8));  // open: dp
  xor xor_1 (xor_1_out, and_3_out, in_1);
  and and_1 (and_1_out, ~H[3], H[2], ~H[1], ~H[0]);  // AND_Gate
  and and_2 (and_2_out, H2[1], ~H2[0]);  // AND_Gate
  lut_BCD_7seg lut_bcd_7seg_5 (
    .out_2(lut_bcd_7seg_5_out_2), .out_3(lut_bcd_7seg_5_out_3), .out_4(lut_bcd_7seg_5_out_4),
    .out_5(lut_bcd_7seg_5_out_5), .out_6(lut_bcd_7seg_5_out_6), .out_7(lut_bcd_7seg_5_out_7),
    .out_8(lut_bcd_7seg_5_out_8), .in_1({1'b0, S2}));
  _7_Segment_Display u_7_segment_display_5 (
    .g(lut_bcd_7seg_5_out_2), .f(lut_bcd_7seg_5_out_3), .a(lut_bcd_7seg_5_out_4), .b(lut_bcd_7seg_5_out_5),
    .e(lut_bcd_7seg_5_out_6), .d(lut_bcd_7seg_5_out_7), .c(lut_bcd_7seg_5_out_8));  // open: dp
  and and_3 (and_3_out, and_1_out, and_2_out);
  lut_BCD_7seg lut_bcd_7seg_6 (
    .out_2(lut_bcd_7seg_6_out_2), .out_3(lut_bcd_7seg_6_out_3), .out_4(lut_bcd_7seg_6_out_4),
    .out_5(lut_bcd_7seg_6_out_5), .out_6(lut_bcd_7seg_6_out_6), .out_7(lut_bcd_7seg_6_out_7),
    .out_8(lut_bcd_7seg_6_out_8), .in_1(S));
  _7_Segment_Display u_7_segment_display_6 (
    .g(lut_bcd_7seg_6_out_2), .f(lut_bcd_7seg_6_out_3), .a(lut_bcd_7seg_6_out_4), .b(lut_bcd_7seg_6_out_5),
    .e(lut_bcd_7seg_6_out_6), .d(lut_bcd_7seg_6_out_7), .c(lut_bcd_7seg_6_out_8));  // open: dp

  // Notes on the sheet:
  //   :
  //   :
endmodule

module lut_BCD_7seg (
  input  [3:0] in_1,
  output out_2,
  output out_3,
  output out_4,
  output out_5,
  output out_6,
  output out_7,
  output out_8
);

  Multiplexer #(.select(4)) multiplexer_1 (
    .in0(1'b0), .in1(1'b0), .in2(1'b1), .in3(1'b1), .in4(1'b1), .in5(1'b1), .in6(1'b1), .in7(1'b0),
    .in8(1'b1), .in9(1'b1), .in10(1'b0), .in11(1'b0), .in12(1'b0), .in13(1'b0), .in14(1'b0), .in15(1'b0),
    .out(out_2), .sel(in_1));  // open: en
  Multiplexer #(.select(4)) multiplexer_2 (
    .in0(1'b1), .in1(1'b0), .in2(1'b0), .in3(1'b0), .in4(1'b1), .in5(1'b1), .in6(1'b1), .in7(1'b0),
    .in8(1'b1), .in9(1'b1), .in10(1'b0), .in11(1'b0), .in12(1'b0), .in13(1'b0), .in14(1'b0), .in15(1'b0),
    .out(out_3), .sel(in_1));  // open: en
  Multiplexer #(.select(4)) multiplexer_3 (
    .in0(1'b1), .in1(1'b0), .in2(1'b1), .in3(1'b1), .in4(1'b0), .in5(1'b1), .in6(1'b1), .in7(1'b1),
    .in8(1'b1), .in9(1'b1), .in10(1'b0), .in11(1'b0), .in12(1'b0), .in13(1'b0), .in14(1'b0), .in15(1'b0),
    .out(out_4), .sel(in_1));  // open: en
  Multiplexer #(.select(4)) multiplexer_4 (
    .in0(1'b1), .in1(1'b1), .in2(1'b1), .in3(1'b1), .in4(1'b1), .in5(1'b0), .in6(1'b0), .in7(1'b1),
    .in8(1'b1), .in9(1'b1), .in10(1'b0), .in11(1'b0), .in12(1'b0), .in13(1'b0), .in14(1'b0), .in15(1'b0),
    .out(out_5), .sel(in_1));  // open: en
  Multiplexer #(.select(4)) multiplexer_5 (
    .in0(1'b1), .in1(1'b0), .in2(1'b1), .in3(1'b0), .in4(1'b0), .in5(1'b0), .in6(1'b1), .in7(1'b0),
    .in8(1'b1), .in9(1'b0), .in10(1'b0), .in11(1'b0), .in12(1'b0), .in13(1'b0), .in14(1'b0), .in15(1'b0),
    .out(out_6), .sel(in_1));  // open: en
  Multiplexer #(.select(4)) multiplexer_6 (
    .in0(1'b1), .in1(1'b0), .in2(1'b1), .in3(1'b1), .in4(1'b0), .in5(1'b1), .in6(1'b1), .in7(1'b0),
    .in8(1'b1), .in9(1'b1), .in10(1'b0), .in11(1'b0), .in12(1'b0), .in13(1'b0), .in14(1'b0), .in15(1'b0),
    .out(out_7), .sel(in_1));  // open: en
  Multiplexer #(.select(4)) multiplexer_7 (
    .in0(1'b1), .in1(1'b1), .in2(1'b0), .in3(1'b1), .in4(1'b1), .in5(1'b1), .in6(1'b1), .in7(1'b1),
    .in8(1'b1), .in9(1'b1), .in10(1'b0), .in11(1'b0), .in12(1'b0), .in13(1'b0), .in14(1'b0), .in15(1'b0),
    .out(out_8), .sel(in_1));  // open: en
  _7_Segment_Display u_7_segment_display_1 (.g(out_2));  // open: f, a, b, e, d, c, dp
  _7_Segment_Display u_7_segment_display_2 (.f(out_3));  // open: g, a, b, e, d, c, dp
  _7_Segment_Display u_7_segment_display_3 (.a(out_4));  // open: g, f, b, e, d, c, dp
  _7_Segment_Display u_7_segment_display_4 (.b(out_5));  // open: g, f, a, e, d, c, dp
  _7_Segment_Display u_7_segment_display_5 (.e(out_6));  // open: g, f, a, b, d, c, dp
  _7_Segment_Display u_7_segment_display_6 (.d(out_7));  // open: g, f, a, b, e, c, dp
  _7_Segment_Display u_7_segment_display_7 (.c(out_8));  // open: g, f, a, b, e, d, dp

  // Other names for the same wires on the sheet: BITS[3:0] = in_1
endmodule

module contador_0___2 (
  input  clock,
  input  clear,
  output Q0,
  output Q1,
  output Q
);

  wire and_1_out, xor_1_out;

  T_Flip_Flop #(.trigger("falling")) t_ff_1 (.clk(clock), .T(1'b1), .Q(Q0), .reset(xor_1_out));  // open: Qn, preset, en
  xor xor_1 (xor_1_out, and_1_out, clear);
  T_Flip_Flop #(.trigger("falling")) t_ff_2 (.clk(Q0), .T(1'b1), .Q(Q), .reset(xor_1_out));  // open: Qn, preset, en
  and and_1 (and_1_out, Q0, Q);

  assign Q1 = Q;
endmodule

module contador_0___5 (
  input  clock,
  input  clear,
  output Q0,
  output Q1,
  output Q2,
  output Q
);

  wire and_1_out, xor_1_out;

  T_Flip_Flop #(.trigger("falling")) t_ff_1 (.clk(clock), .T(1'b1), .Q(Q0), .reset(xor_1_out));  // open: Qn, preset, en
  T_Flip_Flop #(.trigger("falling")) t_ff_2 (.clk(Q0), .T(1'b1), .Q(Q1), .reset(xor_1_out));  // open: Qn, preset, en
  xor xor_1 (xor_1_out, and_1_out, clear);
  T_Flip_Flop #(.trigger("falling")) t_ff_3 (.clk(Q1), .T(1'b1), .Q(Q), .reset(xor_1_out));  // open: Qn, preset, en
  and and_1 (and_1_out, ~Q0, Q1, Q);  // AND_Gate

  assign Q2 = Q;
endmodule

module contador_0___9 (
  input  clock,
  input  clear,
  output Q0,
  output Q1,
  output Q2,
  output Q3,
  output Q
);

  wire and_1_out, xor_1_out;

  T_Flip_Flop #(.trigger("falling")) t_ff_1 (.clk(clock), .T(1'b1), .Q(Q0), .reset(xor_1_out));  // open: Qn, preset, en
  xor xor_1 (xor_1_out, and_1_out, clear);
  T_Flip_Flop #(.trigger("falling")) t_ff_2 (.clk(Q0), .T(1'b1), .Q(Q1), .reset(xor_1_out));  // open: Qn, preset, en
  and and_1 (and_1_out, ~Q0, Q1, ~Q2, Q);  // AND_Gate
  T_Flip_Flop #(.trigger("falling")) t_ff_3 (.clk(Q1), .T(1'b1), .Q(Q2), .reset(xor_1_out));  // open: Qn, preset, en
  T_Flip_Flop #(.trigger("falling")) t_ff_4 (.clk(Q2), .T(1'b1), .Q(Q), .reset(xor_1_out));  // open: Qn, preset, en

  assign Q3 = Q;
endmodule
