// Logisim project trab SD.circ as structural Verilog: 4 circuits, main circuit main
module main (
  input  [7:0] in_1,
  input  [7:0] in_2,
  output [15:0] out_3
);

  wire \multiplicador_mínimo_1_out_7 , \multiplicador_mínimo_2_out_7 , \multiplicador_mínimo_3_out_7 ,
       \multiplicador_mínimo_4_out_7 , \multiplicador_mínimo_5_out_7 , \multiplicador_mínimo_6_out_7 ,
       \multiplicador_mínimo_7_out_7 , \multiplicador_mínimo_9_out_7 , \multiplicador_mínimo_10_out_7 ,
       \multiplicador_mínimo_11_out_7 , \multiplicador_mínimo_12_out_7 , \multiplicador_mínimo_13_out_7 ,
       \multiplicador_mínimo_14_out_7 , \multiplicador_mínimo_15_out_7 , \multiplicador_mínimo_17_out_7 ,
       \multiplicador_mínimo_18_out_7 , \multiplicador_mínimo_19_out_7 , \multiplicador_mínimo_20_out_7 ,
       \multiplicador_mínimo_21_out_7 , \multiplicador_mínimo_22_out_7 , \multiplicador_mínimo_23_out_7 ,
       \multiplicador_mínimo_25_out_7 , \multiplicador_mínimo_26_out_7 , \multiplicador_mínimo_27_out_7 ,
       \multiplicador_mínimo_28_out_7 , \multiplicador_mínimo_29_out_7 , \multiplicador_mínimo_30_out_7 ,
       \multiplicador_mínimo_31_out_7 , somador_completo_1_cout, somador_completo_2_cout,
       somador_completo_3_cout, somador_completo_4_cout, somador_completo_5_cout, somador_completo_6_cout,
       somador_completo_7_cout, somador_completo_8_cout, somador_completo_9_cout, somador_completo_11_cout,
       somador_completo_12_cout, somador_completo_13_cout, somador_completo_14_cout,
       somador_completo_15_cout, somador_completo_16_cout, somador_completo_17_cout,
       somador_completo_18_cout, somador_completo_19_cout, somador_completo_21_cout,
       somador_completo_22_cout, somador_completo_23_cout, somador_completo_24_cout,
       somador_completo_25_cout, somador_completo_26_cout, somador_completo_27_cout,
       somador_completo_28_cout, somador_completo_29_cout, somador_completo_30_cout, somador_completo_31_cout;
  wire [9:2] C;
  wire [11:2] D;
  wire [11:4] G;
  wire [13:4] E;
  wire [15:6] F, H;

  and and_1 (out_3[0], in_1[0], in_2[0]);
  \multiplicador_mínimo  \multiplicador_mínimo_1  (
    .in_3(in_1[1]), .in_4(in_1[0]), .in_5(in_2[1]), .out_6(out_3[1]), .in_1(1'b0),
    .out_7(\multiplicador_mínimo_1_out_7 ), .in_2(in_2[0]));
  \multiplicador_mínimo  \multiplicador_mínimo_2  (
    .in_3(in_1[2]), .in_4(in_1[1]), .in_5(in_2[1]), .out_6(C[2]), .in_1(\multiplicador_mínimo_1_out_7 ),
    .out_7(\multiplicador_mínimo_2_out_7 ), .in_2(in_2[0]));
  \multiplicador_mínimo  \multiplicador_mínimo_3  (
    .in_3(in_1[3]), .in_4(in_1[2]), .in_5(in_2[1]), .out_6(C[3]), .in_1(\multiplicador_mínimo_2_out_7 ),
    .out_7(\multiplicador_mínimo_3_out_7 ), .in_2(in_2[0]));
  \multiplicador_mínimo  \multiplicador_mínimo_4  (
    .in_3(in_1[4]), .in_4(in_1[3]), .in_5(in_2[1]), .out_6(C[4]), .in_1(\multiplicador_mínimo_3_out_7 ),
    .out_7(\multiplicador_mínimo_4_out_7 ), .in_2(in_2[0]));
  \multiplicador_mínimo  \multiplicador_mínimo_5  (
    .in_3(in_1[5]), .in_4(in_1[4]), .in_5(in_2[1]), .out_6(C[5]), .in_1(\multiplicador_mínimo_4_out_7 ),
    .out_7(\multiplicador_mínimo_5_out_7 ), .in_2(in_2[0]));
  \multiplicador_mínimo  \multiplicador_mínimo_6  (
    .in_3(in_1[6]), .in_4(in_1[5]), .in_5(in_2[1]), .out_6(C[6]), .in_1(\multiplicador_mínimo_5_out_7 ),
    .out_7(\multiplicador_mínimo_6_out_7 ), .in_2(in_2[0]));
  \multiplicador_mínimo  \multiplicador_mínimo_7  (
    .in_3(in_1[7]), .in_4(in_1[6]), .in_5(in_2[1]), .out_6(C[7]), .in_1(\multiplicador_mínimo_6_out_7 ),
    .out_7(\multiplicador_mínimo_7_out_7 ), .in_2(in_2[0]));
  \multiplicador_mínimo  \multiplicador_mínimo_8  (
    .in_3(in_1[6]), .in_4(1'b0), .in_5(1'b0), .out_6(C[8]), .in_1(\multiplicador_mínimo_7_out_7 ),
    .out_7(C[9]), .in_2(in_2[0]));
  and and_2 (D[2], in_1[0], in_2[2]);
  \multiplicador_mínimo  \multiplicador_mínimo_9  (
    .in_3(in_1[1]), .in_4(in_1[0]), .in_5(in_2[3]), .out_6(D[3]), .in_1(1'b0),
    .out_7(\multiplicador_mínimo_9_out_7 ), .in_2(in_2[2]));
  \multiplicador_mínimo  \multiplicador_mínimo_10  (
    .in_3(in_1[2]), .in_4(in_1[1]), .in_5(in_2[3]), .out_6(D[4]), .in_1(\multiplicador_mínimo_9_out_7 ),
    .out_7(\multiplicador_mínimo_10_out_7 ), .in_2(in_2[2]));
  \multiplicador_mínimo  \multiplicador_mínimo_11  (
    .in_3(in_1[3]), .in_4(in_1[2]), .in_5(in_2[3]), .out_6(D[5]), .in_1(\multiplicador_mínimo_10_out_7 ),
    .out_7(\multiplicador_mínimo_11_out_7 ), .in_2(in_2[2]));
  \multiplicador_mínimo  \multiplicador_mínimo_12  (
    .in_3(in_1[4]), .in_4(in_1[3]), .in_5(in_2[3]), .out_6(D[6]), .in_1(\multiplicador_mínimo_11_out_7 ),
    .out_7(\multiplicador_mínimo_12_out_7 ), .in_2(in_2[2]));
  \multiplicador_mínimo  \multiplicador_mínimo_13  (
    .in_3(in_1[5]), .in_4(in_1[4]), .in_5(in_2[3]), .out_6(D[7]), .in_1(\multiplicador_mínimo_12_out_7 ),
    .out_7(\multiplicador_mínimo_13_out_7 ), .in_2(in_2[2]));
  \multiplicador_mínimo  \multiplicador_mínimo_14  (
    .in_3(in_1[6]), .in_4(in_1[5]), .in_5(in_2[3]), .out_6(D[8]), .in_1(\multiplicador_mínimo_13_out_7 ),
    .out_7(\multiplicador_mínimo_14_out_7 ), .in_2(in_2[2]));
  \multiplicador_mínimo  \multiplicador_mínimo_15  (
    .in_3(in_1[7]), .in_4(in_1[6]), .in_5(in_2[3]), .out_6(D[9]), .in_1(\multiplicador_mínimo_14_out_7 ),
    .out_7(\multiplicador_mínimo_15_out_7 ), .in_2(in_2[2]));
  \multiplicador_mínimo  \multiplicador_mínimo_16  (
    .in_3(in_1[6]), .in_4(1'b0), .in_5(1'b0), .out_6(D[10]), .in_1(\multiplicador_mínimo_15_out_7 ),
    .out_7(D[11]), .in_2(in_2[2]));
  and and_3 (E[4], in_1[0], in_2[4]);
  \multiplicador_mínimo  \multiplicador_mínimo_17  (
    .in_3(in_1[1]), .in_4(in_1[0]), .in_5(in_2[5]), .out_6(E[5]), .in_1(1'b0),
    .out_7(\multiplicador_mínimo_17_out_7 ), .in_2(in_2[4]));
  \multiplicador_mínimo  \multiplicador_mínimo_18  (
    .in_3(in_1[2]), .in_4(in_1[1]), .in_5(in_2[5]), .out_6(E[6]), .in_1(\multiplicador_mínimo_17_out_7 ),
    .out_7(\multiplicador_mínimo_18_out_7 ), .in_2(in_2[4]));
  \multiplicador_mínimo  \multiplicador_mínimo_19  (
    .in_3(in_1[3]), .in_4(in_1[2]), .in_5(in_2[5]), .out_6(E[7]), .in_1(\multiplicador_mínimo_18_out_7 ),
    .out_7(\multiplicador_mínimo_19_out_7 ), .in_2(in_2[4]));
  \multiplicador_mínimo  \multiplicador_mínimo_20  (
    .in_3(in_1[4]), .in_4(in_1[3]), .in_5(in_2[5]), .out_6(E[8]), .in_1(\multiplicador_mínimo_19_out_7 ),
    .out_7(\multiplicador_mínimo_20_out_7 ), .in_2(in_2[4]));
  \multiplicador_mínimo  \multiplicador_mínimo_21  (
    .in_3(in_1[5]), .in_4(in_1[4]), .in_5(in_2[5]), .out_6(E[9]), .in_1(\multiplicador_mínimo_20_out_7 ),
    .out_7(\multiplicador_mínimo_21_out_7 ), .in_2(in_2[4]));
  \multiplicador_mínimo  \multiplicador_mínimo_22  (
    .in_3(in_1[6]), .in_4(in_1[5]), .in_5(in_2[5]), .out_6(E[10]), .in_1(\multiplicador_mínimo_21_out_7 ),
    .out_7(\multiplicador_mínimo_22_out_7 ), .in_2(in_2[4]));
  \multiplicador_mínimo  \multiplicador_mínimo_23  (
    .in_3(in_1[7]), .in_4(in_1[6]), .in_5(in_2[5]), .out_6(E[11]), .in_1(\multiplicador_mínimo_22_out_7 ),
    .out_7(\multiplicador_mínimo_23_out_7 ), .in_2(in_2[4]));
  \multiplicador_mínimo  \multiplicador_mínimo_24  (
    .in_3(in_1[6]), .in_4(1'b0), .in_5(1'b0), .out_6(E[12]), .in_1(\multiplicador_mínimo_23_out_7 ),
    .out_7(E[13]), .in_2(in_2[4]));
  and and_4 (F[6], in_1[0], in_2[6]);
  \multiplicador_mínimo  \multiplicador_mínimo_25  (
    .in_3(in_1[1]), .in_4(in_1[0]), .in_5(in_2[7]), .out_6(F[7]), .in_1(1'b0),
    .out_7(\multiplicador_mínimo_25_out_7 ), .in_2(in_2[6]));
  \multiplicador_mínimo  \multiplicador_mínimo_26  (
    .in_3(in_1[2]), .in_4(in_1[1]), .in_5(in_2[7]), .out_6(F[8]), .in_1(\multiplicador_mínimo_25_out_7 ),
    .out_7(\multiplicador_mínimo_26_out_7 ), .in_2(in_2[6]));
  \multiplicador_mínimo  \multiplicador_mínimo_27  (
    .in_3(in_1[3]), .in_4(in_1[2]), .in_5(in_2[7]), .out_6(F[9]), .in_1(\multiplicador_mínimo_26_out_7 ),
    .out_7(\multiplicador_mínimo_27_out_7 ), .in_2(in_2[6]));
  \multiplicador_mínimo  \multiplicador_mínimo_28  (
    .in_3(in_1[4]), .in_4(in_1[3]), .in_5(in_2[7]), .out_6(F[10]), .in_1(\multiplicador_mínimo_27_out_7 ),
    .out_7(\multiplicador_mínimo_28_out_7 ), .in_2(in_2[6]));
  \multiplicador_mínimo  \multiplicador_mínimo_29  (
    .in_3(in_1[5]), .in_4(in_1[4]), .in_5(in_2[7]), .out_6(F[11]), .in_1(\multiplicador_mínimo_28_out_7 ),
    .out_7(\multiplicador_mínimo_29_out_7 ), .in_2(in_2[6]));
  \multiplicador_mínimo  \multiplicador_mínimo_30  (
    .in_3(in_1[6]), .in_4(in_1[5]), .in_5(in_2[7]), .out_6(F[12]), .in_1(\multiplicador_mínimo_29_out_7 ),
    .out_7(\multiplicador_mínimo_30_out_7 ), .in_2(in_2[6]));
  \multiplicador_mínimo  \multiplicador_mínimo_31  (
    .in_3(in_1[7]), .in_4(in_1[6]), .in_5(in_2[7]), .out_6(F[13]), .in_1(\multiplicador_mínimo_30_out_7 ),
    .out_7(\multiplicador_mínimo_31_out_7 ), .in_2(in_2[6]));
  \multiplicador_mínimo  \multiplicador_mínimo_32  (
    .in_3(in_1[6]), .in_4(1'b0), .in_5(1'b0), .out_6(F[14]), .in_1(\multiplicador_mínimo_31_out_7 ),
    .out_7(F[15]), .in_2(in_2[6]));
  somador_completo somador_completo_1 (.Cin(1'b0), .A(C[2]), .B(D[2]), .S(out_3[2]), .Cout(somador_completo_1_cout));
  somador_completo somador_completo_2 (
    .Cin(somador_completo_1_cout), .A(C[3]), .B(D[3]), .S(out_3[3]), .Cout(somador_completo_2_cout));
  somador_completo somador_completo_3 (
    .Cin(somador_completo_2_cout), .A(C[4]), .B(D[4]), .S(G[4]), .Cout(somador_completo_3_cout));
  somador_completo somador_completo_4 (
    .Cin(somador_completo_3_cout), .A(C[5]), .B(D[5]), .S(G[5]), .Cout(somador_completo_4_cout));
  somador_completo somador_completo_5 (
    .Cin(somador_completo_4_cout), .A(C[6]), .B(D[6]), .S(G[6]), .Cout(somador_completo_5_cout));
  somador_completo somador_completo_6 (
    .Cin(somador_completo_5_cout), .A(C[7]), .B(D[7]), .S(G[7]), .Cout(somador_completo_6_cout));
  somador_completo somador_completo_7 (
    .Cin(somador_completo_6_cout), .A(C[8]), .B(D[8]), .S(G[8]), .Cout(somador_completo_7_cout));
  somador_completo somador_completo_8 (
    .Cin(somador_completo_7_cout), .A(C[9]), .B(D[9]), .S(G[9]), .Cout(somador_completo_8_cout));
  somador_completo somador_completo_9 (
    .Cin(somador_completo_8_cout), .A(1'b0), .B(D[10]), .S(G[10]), .Cout(somador_completo_9_cout));
  somador_completo somador_completo_10 (.Cin(somador_completo_9_cout), .A(1'b0), .B(D[11]), .S(G[11]));  // open: Cout
  somador_completo somador_completo_11 (.Cin(1'b0), .A(E[6]), .B(F[6]), .S(H[6]), .Cout(somador_completo_11_cout));
  somador_completo somador_completo_12 (
    .Cin(somador_completo_11_cout), .A(E[7]), .B(F[7]), .S(H[7]), .Cout(somador_completo_12_cout));
  somador_completo somador_completo_13 (
    .Cin(somador_completo_12_cout), .A(E[8]), .B(F[8]), .S(H[8]), .Cout(somador_completo_13_cout));
  somador_completo somador_completo_14 (
    .Cin(somador_completo_13_cout), .A(E[9]), .B(F[9]), .S(H[9]), .Cout(somador_completo_14_cout));
  somador_completo somador_completo_15 (
    .Cin(somador_completo_14_cout), .A(E[10]), .B(F[10]), .S(H[10]), .Cout(somador_completo_15_cout));
  somador_completo somador_completo_16 (
    .Cin(somador_completo_15_cout), .A(E[11]), .B(F[11]), .S(H[11]), .Cout(somador_completo_16_cout));
  somador_completo somador_completo_17 (
    .Cin(somador_completo_16_cout), .A(E[12]), .B(F[12]), .S(H[12]), .Cout(somador_completo_17_cout));
  somador_completo somador_completo_18 (
    .Cin(somador_completo_17_cout), .A(E[13]), .B(F[13]), .S(H[13]), .Cout(somador_completo_18_cout));
  somador_completo somador_completo_19 (
    .Cin(somador_completo_18_cout), .A(1'b0), .B(F[14]), .S(H[14]), .Cout(somador_completo_19_cout));
  somador_completo somador_completo_20 (.Cin(somador_completo_19_cout), .A(1'b0), .B(F[15]), .S(H[15]));  // open: Cout
  somador_completo somador_completo_21 (.Cin(1'b0), .A(G[4]), .B(E[4]), .S(out_3[4]), .Cout(somador_completo_21_cout));
  somador_completo somador_completo_22 (
    .Cin(somador_completo_21_cout), .A(G[5]), .B(E[5]), .S(out_3[5]), .Cout(somador_completo_22_cout));
  somador_completo somador_completo_23 (
    .Cin(somador_completo_22_cout), .A(G[6]), .B(H[6]), .S(out_3[6]), .Cout(somador_completo_23_cout));
  somador_completo somador_completo_24 (
    .Cin(somador_completo_23_cout), .A(G[7]), .B(H[7]), .S(out_3[7]), .Cout(somador_completo_24_cout));
  somador_completo somador_completo_25 (
    .Cin(somador_completo_24_cout), .A(G[8]), .B(H[8]), .S(out_3[8]), .Cout(somador_completo_25_cout));
  somador_completo somador_completo_26 (
    .Cin(somador_completo_25_cout), .A(G[9]), .B(H[9]), .S(out_3[9]), .Cout(somador_completo_26_cout));
  somador_completo somador_completo_27 (
    .Cin(somador_completo_26_cout), .A(G[10]), .B(H[10]), .S(out_3[10]), .Cout(somador_completo_27_cout));
  somador_completo somador_completo_28 (
    .Cin(somador_completo_27_cout), .A(G[11]), .B(H[11]), .S(out_3[11]), .Cout(somador_completo_28_cout));
  somador_completo somador_completo_29 (
    .Cin(somador_completo_28_cout), .A(1'b0), .B(H[12]), .S(out_3[12]), .Cout(somador_completo_29_cout));
  somador_completo somador_completo_30 (
    .Cin(somador_completo_29_cout), .A(1'b0), .B(H[13]), .S(out_3[13]), .Cout(somador_completo_30_cout));
  somador_completo somador_completo_31 (
    .Cin(somador_completo_30_cout), .A(1'b0), .B(H[14]), .S(out_3[14]), .Cout(somador_completo_31_cout));
  somador_completo somador_completo_32 (
    .Cin(somador_completo_31_cout), .A(1'b0), .B(H[15]), .S(out_3[15]));  // open: Cout

  // Other names for the same wires on the sheet: A[7:0] = in_1; a0 = in_1[0]; a1 = in_1[1]; a2 = in_1[2];
  //   a3 = in_1[3]; a4 = in_1[4]; a5 = in_1[5]; a6 = in_1[6]; a7 = in_1[7]; B[7:0] = in_2; b0 = in_2[0]; b1 = in_2[1];
  //   b2 = in_2[2]; b3 = in_2[3]; b4 = in_2[4]; b5 = in_2[5]; b6 = in_2[6]; b7 = in_2[7]; H[5:4] = E[5:4]; h4 = E[4];
  //   h5 = E[5]; C[1:0] = out_3[1:0]; c0 = out_3[0]; G[3:0] = out_3[3:0]; g0 = out_3[0]; Resultado[15:0] = out_3;
  //   c1 = out_3[1]; g1 = out_3[1]; g2 = out_3[2]; g3 = out_3[3]
endmodule

module meio_somador (
  input  A,
  input  B,
  output S,
  output Cout
);

  xor xor_1 (S, A, B);
  and and_1 (Cout, A, B);
endmodule

module somador_completo (
  input  Cin,
  input  A,
  input  B,
  output S,
  output Cout
);

  wire meio_somador_1_cout, meio_somador_2_cout, meio_somador_2_s;

  meio_somador meio_somador_1 (.A(Cin), .B(meio_somador_2_s), .S(S), .Cout(meio_somador_1_cout));
  meio_somador meio_somador_2 (.A(A), .B(B), .S(meio_somador_2_s), .Cout(meio_somador_2_cout));
  or or_1 (Cout, meio_somador_1_cout, meio_somador_2_cout);
endmodule

module \multiplicador_mínimo  (
  input  in_1,
  input  in_2,
  input  in_3,
  input  in_4,
  input  in_5,
  output out_6,
  output out_7
);

  wire and_1_out, and_2_out;

  and and_1 (and_1_out, in_2, in_3);
  and and_2 (and_2_out, in_4, in_5);
  somador_completo somador_completo_1 (.Cin(in_1), .A(and_1_out), .B(and_2_out), .S(out_6), .Cout(out_7));
endmodule
